// Logisim project branch.snapshot.circ as structural Verilog: 3 circuits, main circuit main
module main (
  input  in_1
);

  wire clk, detect_end_1_halt, eq, ld_en, lt, pc_sel, reset, rf_we, sw_en;
  wire [1:0] op1_sel;
  wire [2:0] alu_fun, op2_sel, wb_sel;
  wire [4:0] inst_decoder_1_rd, inst_decoder_1_rs1, inst_decoder_1_rs2;
  wire [31:0] adder_1_out, alu_1_p4, data_ram_dout, i_im, inst_mem_data, multiplexer_1_out,
       multiplexer_2_out, multiplexer_3_out, multiplexer_4_out, pc, rf32_1_p5, rf32_1_p18, s_im, sb_im, u_im,
       undriven, x0, x1, x2, x3, x4, x5, x6, x7, x8, x9, x10;

  Clock clock_1 (.out(clk));
  Multiplexer #(.width(32)) multiplexer_1 (
    .in0(multiplexer_2_out), .in1({32{1'b0}}), .out(multiplexer_1_out), .sel(reset));
  Register #(.width(32)) register_1 (.D(multiplexer_1_out), .en(1'b1), .clk(clk), .Q(pc));  // open: clr
  Multiplexer #(.width(32)) multiplexer_2 (.in0(adder_1_out), .in1(rf32_1_p5), .out(multiplexer_2_out), .sel(pc_sel));
  Adder #(.width(32)) adder_1 (.a(32'h4), .b(pc), .out(adder_1_out));  // open: cin, cout
  ROM #(.addrWidth(14), .dataWidth(32)) inst_mem (.addr(pc[15:2]), .data(inst_mem_data));
  detect_end detect_end_1 (.inst(inst_mem_data), .halt(detect_end_1_halt));
  inst_decoder inst_decoder_1 (
    .inst(inst_mem_data), .eq(eq), .lt(lt), .rs1(inst_decoder_1_rs1), .rs2(inst_decoder_1_rs2),
    .rd(inst_decoder_1_rd), .alu_fun(alu_fun), .wb_sel(wb_sel), .op1_sel(op1_sel), .op2_sel(op2_sel),
    .ld_en(ld_en), .sw_en(sw_en), .pc_sel(pc_sel), .rf_we(rf_we), .s_im(s_im), .sb_im(sb_im), .i_im(i_im),
    .u_im(u_im), .j_im(u_im));
  or or_1 (reset, detect_end_1_halt, in_1);
  // Probe on x0
  // Probe on x1
  // Probe on x2
  // Probe on x3
  // rf32 rf32_1: pin names not known; wires that end beside it: inst_decoder_1_rs1, inst_decoder_1_rs2, inst_decoder_1_rd, rf_we, rf32_1_p5, clk, x0, x1, x2, x3, x4, x5, x6, x7, x8, x9, x10, rf32_1_p18
  // Probe on x4
  // Probe on x5
  // Probe on x6
  // Probe on x7
  // Probe on x8
  Multiplexer #(.select(2), .width(32)) multiplexer_3 (
    .in0(rf32_1_p18), .in1(pc), .out(multiplexer_3_out), .sel(op1_sel));  // open: in2, in3
  Multiplexer #(.select(3), .width(32)) multiplexer_4 (
    .in0(undriven), .in1(i_im), .in2(u_im), .in3(s_im), .in4(sb_im), .out(multiplexer_4_out), .sel(op2_sel));  // open: in5, in6, in7
  Comparator #(.width(32)) comparator_1 (.a(rf32_1_p18), .b(undriven), .eq(eq), .lt(lt));  // open: gt
  // alu alu_1: pin names not known; wires that end beside it: multiplexer_3_out, multiplexer_4_out, alu_fun, alu_1_p4
  RAM #(.addrWidth(14), .asyncread("true"), .dataWidth(32)) data_ram (
    .addr(alu_1_p4[15:2]), .we(sw_en), .oe(ld_en), .clk(clk), .din(undriven), .dout(data_ram_dout));
  Multiplexer #(.select(3), .width(32)) multiplexer_5 (
    .in0(alu_1_p4), .in1(data_ram_dout), .out(rf32_1_p5), .sel(wb_sel));  // open: in2, in3, in4, in5, in6, in7

  // Notes on the sheet:
  //   contents of inst_mem (hex, n*v repeats v):
  //   500113 700193 10213 21de63 13 13 100073 badbad0 13 13 415e63 13 13 100073 badbad0 13 13 100073
  //   88888888
endmodule

module detect_end (
  input  [31:0] inst,
  output halt
);

  Comparator #(.mode("unsigned"), .width(32)) comparator_1 (.a(inst), .b(32'h100073), .eq(halt));  // open: gt, lt

  // Notes on the sheet:
  //   ebreak
endmodule

module inst_decoder (
  input  [31:0] inst,
  input  eq,
  input  lt,
  output [4:0] rs1,
  output [4:0] rs2,
  output [4:0] rd,
  output [2:0] alu_fun,
  output [2:0] wb_sel,
  output [1:0] op1_sel,
  output [2:0] op2_sel,
  output ld_en,
  output sw_en,
  output pc_sel,
  output rf_we,
  output [31:0] s_im,
  output [31:0] sb_im,
  output [31:0] i_im,
  output [31:0] u_im,
  output [31:0] j_im
);

  wire add, addi, addr, \and , and_1_out, and_2_out, and_3_out, and_4_out, auipc, beq, bge, blt, bne, branch,
       comparator_1_eq, comparator_2_eq, comparator_3_eq, comparator_4_eq, comparator_5_eq, comparator_6_eq,
       comparator_7_eq, comparator_8_eq, comparator_9_eq, comparator_10_eq, comparator_11_eq,
       comparator_12_eq, comparator_13_eq, comparator_14_eq, comparator_15_eq, comparator_16_eq,
       comparator_17_eq, comparator_18_eq, comparator_22_eq, comparator_23_eq, comparator_24_eq,
       comparator_25_eq, itype, lui, not_1_out, not_2_out, \or , rtype, sub, utype;

  not not_1 (not_1_out, eq);
  not not_2 (not_2_out, lt);
  Comparator #(.width(7)) comparator_1 (.a(inst[6:0]), .b(7'b0110011), .eq(comparator_1_eq));  // open: gt, lt
  Comparator #(.width(3)) comparator_2 (.a(inst[14:12]), .b(3'b000), .eq(comparator_2_eq));  // open: gt, lt
  Comparator #(.width(7)) comparator_3 (.a(inst[31:25]), .b({7{1'b0}}), .eq(comparator_3_eq));  // open: gt, lt
  Comparator #(.width(7)) comparator_4 (.a(inst[6:0]), .b(7'b0110011), .eq(comparator_4_eq));  // open: gt, lt
  Comparator #(.width(3)) comparator_5 (.a(inst[14:12]), .b(3'b000), .eq(comparator_5_eq));  // open: gt, lt
  Comparator #(.width(7)) comparator_6 (.a(inst[31:25]), .b(7'b0100000), .eq(comparator_6_eq));  // open: gt, lt
  Comparator #(.width(7)) comparator_7 (.a(inst[6:0]), .b(7'b0110011), .eq(comparator_7_eq));  // open: gt, lt
  Comparator #(.width(3)) comparator_8 (.a(inst[14:12]), .b(3'b111), .eq(comparator_8_eq));  // open: gt, lt
  Comparator #(.width(7)) comparator_9 (.a(inst[31:25]), .b({7{1'b0}}), .eq(comparator_9_eq));  // open: gt, lt
  Comparator #(.width(7)) comparator_10 (.a(inst[6:0]), .b(7'b0110011), .eq(comparator_10_eq));  // open: gt, lt
  Comparator #(.width(3)) comparator_11 (.a(inst[14:12]), .b(3'b110), .eq(comparator_11_eq));  // open: gt, lt
  Comparator #(.width(7)) comparator_12 (.a(inst[31:25]), .b({7{1'b0}}), .eq(comparator_12_eq));  // open: gt, lt
  Comparator #(.width(7)) comparator_13 (.a(inst[6:0]), .b(7'b0010011), .eq(comparator_13_eq));  // open: gt, lt
  Comparator #(.width(3)) comparator_14 (.a(inst[14:12]), .b(3'b000), .eq(comparator_14_eq));  // open: gt, lt
  Comparator #(.width(7)) comparator_15 (.a(inst[6:0]), .b(7'b0000011), .eq(comparator_15_eq));  // open: gt, lt
  Comparator #(.width(3)) comparator_16 (.a(inst[14:12]), .b(3'b010), .eq(comparator_16_eq));  // open: gt, lt
  Comparator #(.width(7)) comparator_17 (.a(inst[6:0]), .b(7'b0100011), .eq(comparator_17_eq));  // open: gt, lt
  Comparator #(.width(3)) comparator_18 (.a(inst[14:12]), .b(3'b010), .eq(comparator_18_eq));  // open: gt, lt
  Comparator #(.width(7)) comparator_19 (.a(inst[6:0]), .b(7'b0110111), .eq(lui));  // open: gt, lt
  Comparator #(.width(7)) comparator_20 (.a(inst[6:0]), .b(7'b0010111), .eq(auipc));  // open: gt, lt
  Comparator #(.width(7)) comparator_21 (.a(inst[6:0]), .b(7'b1100011), .eq(branch));  // open: gt, lt
  Comparator #(.width(3)) comparator_22 (.a(inst[14:12]), .b(3'b000), .eq(comparator_22_eq));  // open: gt, lt
  Comparator #(.width(3)) comparator_23 (.a(inst[14:12]), .b(3'b001), .eq(comparator_23_eq));  // open: gt, lt
  Comparator #(.width(3)) comparator_24 (.a(inst[14:12]), .b(3'b100), .eq(comparator_24_eq));  // open: gt, lt
  Comparator #(.width(3)) comparator_25 (.a(inst[14:12]), .b(3'b101), .eq(comparator_25_eq));  // open: gt, lt
  and and_1 (and_1_out, beq, eq);
  and and_2 (and_2_out, bne, not_1_out);
  and and_3 (and_3_out, blt, lt);
  and and_4 (and_4_out, bge, not_2_out);
  assign i_im[31:11] = {{20{inst[31]}}, inst[31]};  // Bit_Extender bit_extender_1
  assign sb_im[31:12] = {{19{inst[31]}}, inst[31]};  // Bit_Extender bit_extender_2
  and and_5 (addr, comparator_1_eq, comparator_2_eq, comparator_3_eq);
  and and_6 (sub, comparator_4_eq, comparator_5_eq, comparator_6_eq);
  and and_7 (\and , comparator_7_eq, comparator_8_eq, comparator_9_eq);
  and and_8 (\or , comparator_10_eq, comparator_11_eq, comparator_12_eq);
  and and_9 (addi, comparator_13_eq, comparator_14_eq);
  and and_10 (ld_en, comparator_15_eq, comparator_16_eq);
  and and_11 (sw_en, comparator_17_eq, comparator_18_eq);
  and and_12 (beq, branch, comparator_22_eq);
  and and_13 (bne, branch, comparator_23_eq);
  and and_14 (blt, branch, comparator_24_eq);
  and and_15 (bge, branch, comparator_25_eq);
  or or_1 (pc_sel, and_1_out, and_2_out, 1'b0, 1'b0, and_3_out, and_4_out);
  or or_2 (add, addr, addi, auipc, branch, ld_en, lui, 1'b0);
  or or_3 (rtype, addr, sub, \and , \or );
  or or_4 (itype, addi, ld_en);
  or or_5 (utype, lui, auipc);
  or or_6 (op1_sel[0], auipc, branch);
  Priority_Encoder priority_encoder_1 (
    .in0(sub), .in1(add), .in2(\or ), .in3(\and ), .in4(1'b0), .in5(1'b0), .in6(1'b0), .in7(1'b0),
    .out(alu_fun), .en_in(1'b1));  // open: gs, en_out
  Multiplexer #(.width(5)) multiplexer_1 (.in0(inst[19:15]), .in1({5{1'b0}}), .out(rs1), .sel(utype));
  Priority_Encoder priority_encoder_2 (
    .in0(rtype), .in1(itype), .in2(utype), .in3(sw_en), .in4(branch), .in5(1'b0), .in6(1'b0), .in7(1'b0),
    .out(op2_sel), .en_in(1'b1));  // open: gs, en_out
  not not_3 (rf_we, sw_en);

  assign i_im[10:0] = inst[30:20];
  assign op1_sel[1] = 1'b0;
  assign rd = inst[11:7];
  assign rs2 = inst[24:20];
  assign s_im = {{20{1'b0}}, inst[31:25], inst[11:7]};
  assign sb_im[11:0] = {inst[7], inst[30:25], inst[11:8], 1'b0};
  assign u_im = {inst[31:12], {12{1'b0}}};
  assign wb_sel = {2'b00, ld_en};

  // Other names for the same wires on the sheet: op[6:0] = inst[6:0]; op1_pc = op1_sel[0]; fun7[6:0] = inst[31:25];
  //   sw = sw_en; fun3[2:0] = inst[14:12]; rs1_i[4:0] = inst[19:15]; lw = ld_en
endmodule
