// Logisim project rv32_all.circ as structural Verilog: 3 circuits, main circuit main
module main (
  output reset,
  output [31:0] out_2,
  output [31:0] out_3,
  output [31:0] out_4,
  output [31:0] out_5,
  output [31:0] out_6,
  output [31:0] out_7,
  output [31:0] out_8,
  output [31:0] out_9,
  output [31:0] out_10,
  output [31:0] out_11,
  output [31:0] out_12
);

  wire clk, eq, Id_en, lt, rf_we, sw_en;
  wire [1:0] op1_sel, pc_sel;
  wire [2:0] alu_fun, op2_sel, wb_sel;
  wire [4:0] inst_decoder_1_rd, inst_decoder_1_rs1, inst_decoder_1_rs2;
  wire [31:0] data_ram_dout, i_im, inst_mem_data, j_im, jdest, multiplexer_1_out, multiplexer_2_out,
       multiplexer_3_out, next_pc, pc, rf32_1_p5, rf32_1_p18, s_im, sb_im, u_im, undriven;

  Clock clock_1 (.out(clk));
  Register #(.width(32)) register_1 (.D(multiplexer_1_out), .en(1'b1), .clk(clk), .Q(pc));  // open: clr
  Multiplexer #(.select(2), .width(32)) multiplexer_1 (
    .in0(next_pc), .in1(rf32_1_p5), .in2(jdest), .out(multiplexer_1_out), .sel(pc_sel));  // open: in3
  Adder #(.width(32)) adder_1 (.a(32'h4), .b(pc), .out(next_pc));  // open: cin, cout
  ROM #(.addrWidth(14), .dataWidth(32)) inst_mem (.addr(pc[15:2]), .data(inst_mem_data));
  detect_end detect_end_1 (.inst(inst_mem_data), .halt(reset));
  inst_decoder inst_decoder_1 (
    .inst(inst_mem_data), .eq(eq), .lt(lt), .rs1(inst_decoder_1_rs1), .rs2(inst_decoder_1_rs2),
    .rd(inst_decoder_1_rd), .alu_fun(alu_fun), .wb_sel(wb_sel), .op2_sel(op2_sel), .ld_en(Id_en),
    .sw_en(sw_en), .pc_sel(pc_sel), .rf_we(rf_we), .op1_sel(op1_sel), .s_im(s_im), .sb_im(sb_im),
    .i_im(i_im), .u_im(u_im), .j_im(j_im));
  // Probe on out_2
  // Probe on out_3
  // Probe on out_4
  // Probe on out_5
  // rf32 rf32_1: pin names not known; wires that end beside it: inst_decoder_1_rs1, inst_decoder_1_rs2, inst_decoder_1_rd, rf_we, rf32_1_p5, clk, out_2, out_3, out_4, out_5, out_6, out_7, out_8, out_9, out_10, out_11, out_12, rf32_1_p18
  // Probe on out_6
  // Probe on out_7
  // Probe on out_8
  // Probe on out_9
  // Probe on out_10
  Comparator #(.width(32)) comparator_1 (.a(rf32_1_p18), .b(undriven), .eq(eq), .lt(lt));  // open: gt
  Multiplexer #(.select(2), .width(32)) multiplexer_2 (
    .in0(rf32_1_p18), .in1(pc), .out(multiplexer_2_out), .sel(op1_sel));  // open: in2, in3
  Multiplexer #(.select(3), .width(32)) multiplexer_3 (
    .in0(undriven), .in1(i_im), .in2(u_im), .in3(s_im), .in4(sb_im), .in5(j_im), .out(multiplexer_3_out),
    .sel(op2_sel));  // open: in6, in7
  // alu alu_1: pin names not known; wires that end beside it: multiplexer_2_out, multiplexer_3_out, alu_fun, jdest
  RAM #(.addrWidth(14), .asyncread("true"), .dataWidth(32)) data_ram (
    .addr(jdest[15:2]), .we(sw_en), .oe(Id_en), .clk(clk), .din(undriven), .dout(data_ram_dout));
  Multiplexer #(.select(3), .width(32)) multiplexer_4 (
    .in0(jdest), .in1(data_ram_dout), .in2(next_pc), .out(rf32_1_p5), .sel(wb_sel));  // open: in3, in4, in5, in6, in7

  // Other names for the same wires on the sheet: x0[31:0] = out_2; x1[31:0] = out_3; x2[31:0] = out_4;
  //   x3[31:0] = out_5; x4[31:0] = out_6; x5[31:0] = out_7; x6[31:0] = out_8; x7[31:0] = out_9; x8[31:0] = out_10;
  //   x9[31:0] = out_11; x10[31:0] = out_12

  // Notes on the sheet:
  //   contents of inst_mem (hex, n*v repeats v):
  //   200e13 93 24000ef 100073 badbad0 13 3428293 100073 88888888 13 13 c10113 c08267 100073 badbad0
endmodule

module detect_end (
  input  [31:0] inst,
  output halt
);

  Comparator #(.mode("unsigned"), .width(32)) comparator_1 (.a(inst), .b(32'h100073), .eq(halt));  // open: gt, lt

  // Notes on the sheet:
  //   ebreak
endmodule

module inst_decoder (
  input  [31:0] inst,
  input  eq,
  input  lt,
  output [4:0] rs1,
  output [4:0] rs2,
  output [4:0] rd,
  output [2:0] alu_fun,
  output [2:0] wb_sel,
  output [2:0] op2_sel,
  output ld_en,
  output sw_en,
  output [1:0] pc_sel,
  output rf_we,
  output [1:0] op1_sel,
  output [31:0] s_im,
  output [31:0] sb_im,
  output [31:0] i_im,
  output [31:0] u_im,
  output [31:0] j_im
);

  wire add, addi, addr, \and , and_13_out, and_14_out, and_15_out, and_16_out, auipc, beq, bge, blt, bne,
       branch, comparator_3_eq, comparator_4_eq, comparator_5_eq, comparator_6_eq, comparator_7_eq,
       comparator_8_eq, comparator_9_eq, comparator_10_eq, comparator_11_eq, comparator_12_eq,
       comparator_13_eq, comparator_14_eq, comparator_15_eq, comparator_16_eq, comparator_17_eq,
       comparator_18_eq, comparator_19_eq, comparator_20_eq, comparator_21_eq, comparator_22_eq,
       comparator_23_eq, comparator_24_eq, comparator_27_eq, comparator_28_eq, i_type, jal, jalr, lui,
       not_1_out, not_2_out, \or , or_8_out, r_type, sel_pc, sub, u_type, uj;

  Priority_Encoder priority_encoder_1 (
    .in0(sub), .in1(add), .in2(\or ), .in3(\and ), .in4(1'b0), .in5(1'b0), .in6(1'b0), .in7(1'b0),
    .out(alu_fun), .en_in(1'b1));  // open: gs, en_out
  Comparator #(.width(7)) comparator_1 (.a(inst[6:0]), .b(7'b1100011), .eq(branch));  // open: gt, lt
  Comparator #(.width(7)) comparator_2 (.a(inst[6:0]), .b(7'b1101111), .eq(jal));  // open: gt, lt
  Comparator #(.width(7)) comparator_3 (.a(inst[6:0]), .b(7'b1100111), .eq(comparator_3_eq));  // open: gt, lt
  Comparator #(.width(3)) comparator_4 (.a(inst[14:12]), .b(3'b000), .eq(comparator_4_eq));  // open: gt, lt
  or or_1 (uj, jal, jalr);
  Comparator #(.width(7)) comparator_5 (.a(inst[6:0]), .b(7'b0110011), .eq(comparator_5_eq));  // open: gt, lt
  Comparator #(.width(3)) comparator_6 (.a(inst[14:12]), .b(3'b000), .eq(comparator_6_eq));  // open: gt, lt
  Comparator #(.width(7)) comparator_7 (.a(inst[31:25]), .b(7'b0100000), .eq(comparator_7_eq));  // open: gt, lt
  Comparator #(.width(7)) comparator_8 (.a(inst[6:0]), .b(7'b0110011), .eq(comparator_8_eq));  // open: gt, lt
  Comparator #(.width(3)) comparator_9 (.a(inst[14:12]), .b(3'b111), .eq(comparator_9_eq));  // open: gt, lt
  Comparator #(.width(7)) comparator_10 (.a(inst[31:25]), .b({7{1'b0}}), .eq(comparator_10_eq));  // open: gt, lt
  Comparator #(.width(7)) comparator_11 (.a(inst[6:0]), .b(7'b0110011), .eq(comparator_11_eq));  // open: gt, lt
  Comparator #(.width(3)) comparator_12 (.a(inst[14:12]), .b(3'b110), .eq(comparator_12_eq));  // open: gt, lt
  Comparator #(.width(7)) comparator_13 (.a(inst[31:25]), .b({7{1'b0}}), .eq(comparator_13_eq));  // open: gt, lt
  Comparator #(.width(7)) comparator_14 (.a(inst[6:0]), .b(7'b0110011), .eq(comparator_14_eq));  // open: gt, lt
  Comparator #(.width(3)) comparator_15 (.a(inst[14:12]), .b(3'b000), .eq(comparator_15_eq));  // open: gt, lt
  Comparator #(.width(7)) comparator_16 (.a(inst[31:25]), .b({7{1'b0}}), .eq(comparator_16_eq));  // open: gt, lt
  and and_1 (jalr, comparator_3_eq, comparator_4_eq);
  and and_2 (addr, comparator_14_eq, comparator_15_eq, comparator_16_eq);
  or or_2 (u_type, lui, auipc);
  or or_3 (i_type, addi, jalr, ld_en);
  and and_3 (sub, comparator_5_eq, comparator_6_eq, comparator_7_eq);
  and and_4 (\and , comparator_8_eq, comparator_9_eq, comparator_10_eq);
  and and_5 (\or , comparator_11_eq, comparator_12_eq, comparator_13_eq);
  or or_4 (r_type, addr, sub, \and , \or );
  or or_5 (op1_sel[0], auipc, jal, branch, 1'b0);
  or or_6 (add, branch, addr, addi, auipc, ld_en, sw_en, lui, uj);
  Comparator #(.width(3)) comparator_17 (.a(inst[14:12]), .b(3'b000), .eq(comparator_17_eq));  // open: gt, lt
  Comparator #(.width(3)) comparator_18 (.a(inst[14:12]), .b(3'b001), .eq(comparator_18_eq));  // open: gt, lt
  Comparator #(.width(3)) comparator_19 (.a(inst[14:12]), .b(3'b100), .eq(comparator_19_eq));  // open: gt, lt
  Comparator #(.width(3)) comparator_20 (.a(inst[14:12]), .b(3'b101), .eq(comparator_20_eq));  // open: gt, lt
  and and_6 (beq, branch, comparator_17_eq);
  and and_7 (bne, branch, comparator_18_eq);
  and and_8 (blt, branch, comparator_19_eq);
  and and_9 (bge, branch, comparator_20_eq);
  Comparator #(.width(7)) comparator_21 (.a(inst[6:0]), .b(7'b0000011), .eq(comparator_21_eq));  // open: gt, lt
  Comparator #(.width(3)) comparator_22 (.a(inst[14:12]), .b(3'b010), .eq(comparator_22_eq));  // open: gt, lt
  Comparator #(.width(7)) comparator_23 (.a(inst[6:0]), .b(7'b0100011), .eq(comparator_23_eq));  // open: gt, lt
  Comparator #(.width(3)) comparator_24 (.a(inst[14:12]), .b(3'b010), .eq(comparator_24_eq));  // open: gt, lt
  Comparator #(.width(7)) comparator_25 (.a(inst[6:0]), .b(7'b0010111), .eq(auipc));  // open: gt, lt
  Comparator #(.width(7)) comparator_26 (.a(inst[6:0]), .b(7'b0110111), .eq(lui));  // open: gt, lt
  Comparator #(.width(7)) comparator_27 (.a(inst[6:0]), .b(7'b0010011), .eq(comparator_27_eq));  // open: gt, lt
  Comparator #(.width(3)) comparator_28 (.a(inst[14:12]), .b(3'b000), .eq(comparator_28_eq));  // open: gt, lt
  and and_10 (ld_en, comparator_21_eq, comparator_22_eq);
  and and_11 (sw_en, comparator_23_eq, comparator_24_eq);
  and and_12 (addi, comparator_27_eq, comparator_28_eq);
  assign sb_im[31:12] = {{19{inst[31]}}, inst[31]};  // Bit_Extender bit_extender_1
  assign j_im[31:20] = {{11{inst[31]}}, inst[31]};  // Bit_Extender bit_extender_2
  not not_1 (not_1_out, eq);
  not not_2 (not_2_out, lt);
  not not_3 (rf_we, sw_en);
  and and_13 (and_13_out, beq, eq);
  and and_14 (and_14_out, bne, not_1_out);
  and and_15 (and_15_out, blt, lt);
  and and_16 (and_16_out, bge, not_2_out);
  Priority_Encoder priority_encoder_2 (
    .in0(r_type), .in1(i_type), .in2(u_type), .in3(sw_en), .in4(branch), .in5(jal), .in6(1'b0), .in7(1'b0),
    .out(op2_sel), .en_in(1'b1));  // open: gs, en_out
  Multiplexer #(.width(5)) multiplexer_1 (.in0(inst[19:15]), .in1({5{1'b0}}), .out(rs1), .sel(u_type));
  Priority_Encoder #(.select(2)) priority_encoder_3 (
    .in0(1'b1), .in1(sel_pc), .in2(uj), .out(pc_sel), .en_in(1'b1));  // open: in3, gs, en_out
  or or_7 (sel_pc, and_13_out, and_14_out, uj, 1'b0, and_15_out, and_16_out);
  or or_8 (or_8_out, jal, jalr);
  Priority_Encoder priority_encoder_4 (
    .in0(1'b1), .in1(ld_en), .in2(or_8_out), .in3(1'b0), .in4(1'b0), .in5(1'b0), .in6(1'b0), .in7(1'b0),
    .out(wb_sel), .en_in(1'b1));  // open: gs, en_out

  assign i_im = {{21{inst[31]}}, inst[30:20]};
  assign j_im[19:0] = {inst[19:12], inst[20], inst[30:21], 1'b0};
  assign op1_sel[1] = 1'b0;
  assign rd = inst[11:7];
  assign rs2 = inst[24:20];
  assign s_im = {{20{1'b0}}, inst[31:25], inst[11:7]};
  assign sb_im[11:0] = {inst[7], inst[30:25], inst[11:8], 1'b0};
  assign u_im = {inst[31:12], {12{1'b0}}};

  // Other names for the same wires on the sheet: lw = ld_en; op[6:0] = inst[6:0]; op1_pc = op1_sel[0]; sw = sw_en;
  //   fun3[2:0] = inst[14:12]; rs1_i[4:0] = inst[19:15]; fun7[6:0] = inst[31:25]

  // Notes on the sheet:
  //   When the instruction is ADD
  //   When the instruction is SUB
  //   When the instruction is AND
  //   When the instruction is OR
  //   When the instruction is ADDI
endmodule
