// Logisim project rv32_isu.circ as structural Verilog: 3 circuits, main circuit main
module main (
  output [31:0] out_1,
  output [31:0] out_2,
  output [31:0] out_3,
  output [31:0] out_4,
  output [31:0] out_5,
  output [31:0] out_6,
  output [31:0] out_7,
  output [31:0] out_8,
  output [31:0] out_9,
  output [31:0] out_10,
  output [31:0] out_11
);

  wire clk, halt, Id_en, ld_en, rf_we, sw_en;
  wire [1:0] op2_sel, pc_sel;
  wire [2:0] alu_fun, wb_sel;
  wire [4:0] inst_decoder_1_rd, inst_decoder_1_rs1, inst_decoder_1_rs2;
  wire [31:0] adder_1_out, alu_1_p5, data_ram_dout, i_im, inst_mem_data, j_im, multiplexer_1_out,
       multiplexer_2_out, multiplexer_3_out, pc, rf32_1_p5, rf32_1_p18, s_im, sb_im, u_im, undriven;

  Clock clock_1 (.out(clk));
  Multiplexer #(.width(32)) multiplexer_1 (.in0(adder_1_out), .in1({32{1'b0}}), .out(multiplexer_1_out), .sel(halt));
  Register #(.width(32)) register_1 (.D(multiplexer_1_out), .en(1'b1), .clk(clk), .Q(pc));  // open: clr
  Adder #(.width(32)) adder_1 (.a(32'h4), .b(pc), .out(adder_1_out));  // open: cin, cout
  ROM #(.addrWidth(14), .dataWidth(32)) inst_mem (.addr(pc[15:2]), .data(inst_mem_data));
  detect_end detect_end_1 (.inst(inst_mem_data), .halt(halt));
  inst_decoder inst_decoder_1 (
    .in_1(inst_mem_data), .rs1(inst_decoder_1_rs1), .rs2(inst_decoder_1_rs2), .rd(inst_decoder_1_rd),
    .alu_fun(alu_fun), .wb_sel(wb_sel), .op2_sel(op2_sel), .ld_en(Id_en), .sw_en(sw_en), .pc_sel(pc_sel),
    .rf_we(rf_we), .s_im(s_im), .sb_im(sb_im), .i_im(i_im), .u_im(u_im), .j_im(j_im));  // open: br_eq, blt, bge
  // Probe on out_1
  // Probe on out_2
  // Probe on out_3
  // Probe on out_4
  // rf32 rf32_1: pin names not known; wires that end beside it: inst_decoder_1_rs1, inst_decoder_1_rs2, inst_decoder_1_rd, rf_we, rf32_1_p5, clk, out_1, out_2, out_3, out_4, out_5, out_6, out_7, out_8, out_9, out_10, out_11, rf32_1_p18
  // Probe on out_5
  // Probe on out_6
  // Probe on out_7
  // Probe on out_8
  Multiplexer #(.select(2), .width(32)) multiplexer_2 (
    .in0(rf32_1_p18), .in1(pc), .in2({32{1'b0}}), .in3({32{1'b0}}), .out(multiplexer_2_out), .sel(pc_sel));
  // Probe on out_9
  Multiplexer #(.select(2), .width(32)) multiplexer_3 (
    .in0(undriven), .in1(i_im), .in2(u_im), .in3(s_im), .out(multiplexer_3_out), .sel(op2_sel));
  // alu alu_1: pin names not known; wires that end beside it: multiplexer_2_out, multiplexer_3_out, alu_fun, s_im, alu_1_p5
  RAM #(.addrWidth(14), .asyncread("true"), .dataWidth(32)) data_ram (
    .addr(alu_1_p5[15:2]), .we(sw_en), .oe(ld_en), .clk(clk), .din(undriven), .dout(data_ram_dout));
  Multiplexer #(.select(3), .width(32)) multiplexer_4 (
    .in0(alu_1_p5), .in1(data_ram_dout), .out(rf32_1_p5), .sel(wb_sel));  // open: in2, in3, in4, in5, in6, in7

  // Other names for the same wires on the sheet: x0[31:0] = out_1; x1[31:0] = out_2; x2[31:0] = out_3;
  //   x3[31:0] = out_4; x4[31:0] = out_5; x5[31:0] = out_6; x6[31:0] = out_7; x7[31:0] = out_8; x8[31:0] = out_9;
  //   x9[31:0] = out_10; x10[31:0] = out_11

  // Notes on the sheet:
  //   contents of inst_mem (hex, n*v repeats v):
  //   100093 1097 100073
endmodule

module detect_end (
  input  [31:0] inst,
  output halt
);

  Comparator #(.mode("unsigned"), .width(32)) comparator_1 (.a(inst), .b(32'h100073), .eq(halt));  // open: gt, lt

  // Notes on the sheet:
  //   ebreak
endmodule

module inst_decoder (
  input  [31:0] in_1,
  input  br_eq,
  input  blt,
  input  bge,
  output [4:0] rs1,
  output [4:0] rs2,
  output [4:0] rd,
  output [2:0] alu_fun,
  output [2:0] wb_sel,
  output [1:0] op2_sel,
  output ld_en,
  output sw_en,
  output [1:0] pc_sel,
  output rf_we,
  output [31:0] s_im,
  output [31:0] sb_im,
  output [31:0] i_im,
  output [31:0] u_im,
  output [31:0] j_im
);

  wire add, addi, \and , and_1_out, auipc, comparator_1_eq, comparator_2_eq, comparator_3_eq,
       comparator_4_eq, comparator_5_eq, comparator_6_eq, comparator_7_eq, comparator_8_eq, comparator_9_eq,
       comparator_10_eq, comparator_11_eq, comparator_12_eq, comparator_13_eq, comparator_14_eq,
       comparator_15_eq, comparator_16_eq, comparator_19_eq, comparator_20_eq, i_type, lui, \or , or_5_out,
       r_type, sub, u_type;

  Priority_Encoder priority_encoder_1 (
    .in0(sub), .in1(add), .in2(\or ), .in3(\and ), .in4(1'b0), .in5(1'b0), .in6(1'b0), .in7(1'b0),
    .out(alu_fun), .en_in(1'b1));  // open: gs, en_out
  Comparator #(.width(7)) comparator_1 (.a(in_1[6:0]), .b(7'b0110011), .eq(comparator_1_eq));  // open: gt, lt
  Comparator #(.width(3)) comparator_2 (.a(in_1[14:12]), .b(3'b000), .eq(comparator_2_eq));  // open: gt, lt
  Comparator #(.width(7)) comparator_3 (.a(in_1[31:25]), .b({7{1'b0}}), .eq(comparator_3_eq));  // open: gt, lt
  Comparator #(.width(7)) comparator_4 (.a(in_1[6:0]), .b(7'b0110011), .eq(comparator_4_eq));  // open: gt, lt
  Comparator #(.width(3)) comparator_5 (.a(in_1[14:12]), .b(3'b000), .eq(comparator_5_eq));  // open: gt, lt
  Comparator #(.width(7)) comparator_6 (.a(in_1[31:25]), .b(7'b0100000), .eq(comparator_6_eq));  // open: gt, lt
  Comparator #(.width(7)) comparator_7 (.a(in_1[6:0]), .b(7'b0110011), .eq(comparator_7_eq));  // open: gt, lt
  Comparator #(.width(3)) comparator_8 (.a(in_1[14:12]), .b(3'b111), .eq(comparator_8_eq));  // open: gt, lt
  Comparator #(.width(7)) comparator_9 (.a(in_1[31:25]), .b({7{1'b0}}), .eq(comparator_9_eq));  // open: gt, lt
  Comparator #(.width(7)) comparator_10 (.a(in_1[6:0]), .b(7'b0110011), .eq(comparator_10_eq));  // open: gt, lt
  Comparator #(.width(3)) comparator_11 (.a(in_1[14:12]), .b(3'b110), .eq(comparator_11_eq));  // open: gt, lt
  Comparator #(.width(7)) comparator_12 (.a(in_1[31:25]), .b({7{1'b0}}), .eq(comparator_12_eq));  // open: gt, lt
  and and_1 (and_1_out, comparator_1_eq, comparator_2_eq, comparator_3_eq);
  and and_2 (sub, comparator_4_eq, comparator_5_eq, comparator_6_eq);
  and and_3 (\and , comparator_7_eq, comparator_8_eq, comparator_9_eq);
  and and_4 (\or , comparator_10_eq, comparator_11_eq, comparator_12_eq);
  or or_1 (u_type, lui, auipc);
  or or_2 (i_type, addi, ld_en);
  or or_3 (r_type, add, sub, \and , \or );
  or or_4 (add, and_1_out, addi, auipc, ld_en, sw_en, lui);
  Priority_Encoder priority_encoder_2 (
    .in0(1'b1), .in1(ld_en), .out(wb_sel), .en_in(1'b1));  // open: in2, in3, in4, in5, in6, in7, gs, en_out
  Comparator #(.width(7)) comparator_13 (.a(in_1[6:0]), .b(7'b0000011), .eq(comparator_13_eq));  // open: gt, lt
  Comparator #(.width(3)) comparator_14 (.a(in_1[14:12]), .b(3'b010), .eq(comparator_14_eq));  // open: gt, lt
  Comparator #(.width(7)) comparator_15 (.a(in_1[6:0]), .b(7'b0100011), .eq(comparator_15_eq));  // open: gt, lt
  Comparator #(.width(3)) comparator_16 (.a(in_1[14:12]), .b(3'b010), .eq(comparator_16_eq));  // open: gt, lt
  Comparator #(.width(7)) comparator_17 (.a(in_1[6:0]), .b(7'b0010111), .eq(auipc));  // open: gt, lt
  Comparator #(.width(7)) comparator_18 (.a(in_1[6:0]), .b(7'b0110111), .eq(lui));  // open: gt, lt
  Comparator #(.width(7)) comparator_19 (.a(in_1[6:0]), .b(7'b0010011), .eq(comparator_19_eq));  // open: gt, lt
  Comparator #(.width(3)) comparator_20 (.a(in_1[14:12]), .b(3'b000), .eq(comparator_20_eq));  // open: gt, lt
  and and_5 (ld_en, comparator_13_eq, comparator_14_eq);
  and and_6 (sw_en, comparator_15_eq, comparator_16_eq);
  and and_7 (addi, comparator_19_eq, comparator_20_eq);
  Priority_Encoder #(.select(2)) priority_encoder_3 (
    .in0(r_type), .in1(i_type), .in2(u_type), .in3(sw_en), .out(op2_sel), .en_in(1'b1));  // open: gs, en_out
  or or_5 (or_5_out, r_type, i_type);
  not not_1 (rf_we, sw_en);
  Priority_Encoder #(.select(2)) priority_encoder_4 (
    .in0(or_5_out), .in1(auipc), .in2(lui), .in3(1'b0), .out(pc_sel), .en_in(1'b1));  // open: gs, en_out

  assign i_im = {{21{in_1[31]}}, in_1[30:20]};
  assign rd = in_1[11:7];
  assign rs1 = in_1[19:15];
  assign rs2 = in_1[24:20];
  assign s_im = {{20{1'b0}}, in_1[31:25], in_1[11:7]};
  assign u_im = {in_1[31:12], {12{1'b0}}};

  // Other names for the same wires on the sheet: lw = ld_en; inst[31:0] = in_1; op[6:0] = in_1[6:0]; sw = sw_en;
  //   fun3[2:0] = in_1[14:12]; fun7[6:0] = in_1[31:25]

  // Notes on the sheet:
  //   When the instruction is ADD
  //   When the instruction is SUB
  //   When the instruction is AND
  //   When the instruction is OR
  //   When the instruction is ADDI
endmodule
