// Logisim project checkoff1.circ as structural Verilog: 1 circuit, main circuit main
module main (
  input  [31:0] A,
  input  [31:0] B,
  output [7:0] Y
);

  Adder #(.width(32)) adder_1 (.a(A), .b(B));  // open: out, cin, cout
endmodule
