// Logisim project smallacc.circ as structural Verilog: 2 circuits, main circuit main
module main (
  input  [31:0] X,
  output [31:0] Y
);

  wire clk_out;
  wire [31:0] RegisterA_q, RegisterB_q, signext_1_cx;

  Clock clk (.out(clk_out));
  Register #(.width(32)) RegisterA (.D(Y), .en(clk_out), .clk(clk_out), .Q(RegisterA_q));  // open: clr
  Register #(.width(32)) RegisterB (.D(X), .en(clk_out), .clk(clk_out), .Q(RegisterB_q));  // open: clr
  signext signext_1 (.C(RegisterB_q[11:0]), .CX(signext_1_cx));
  Adder #(.width(32)) adder_1 (.a(RegisterA_q), .b(signext_1_cx), .out(Y));  // open: cin, cout
endmodule

module signext (
  input  [11:0] C,
  output [31:0] CX
);

  Multiplexer #(.width(21)) multiplexer_1 (.in0({21{1'b0}}), .in1({21{1'b0}}), .out(CX[31:11]), .sel(C[11]));

  assign CX[10:0] = C[10:0];
endmodule
