// Logisim project lab3_checkpoint1_3035770800.circ as structural Verilog: 1 circuit, main circuit main
module main (
  input  [31:0] A,
  input  [31:0] B,
  output [7:0] Y
);

  wire [31:8] adder_1_out;

  Adder #(.width(32)) adder_1 (.a(A), .b(B), .out({adder_1_out, Y}));  // open: cin, cout
endmodule
